// Logisim project marde.circ as structural Verilog: 1 circuit, main circuit main
module main (
);

  wire and_1_out, clock_1_out;
  wire [7:0] counter_1_q;

  Clock clock_1 (.out(clock_1_out));
  Counter counter_1 (.clr(and_1_out), .up(1'b1), .clk(clock_1_out), .Q(counter_1_q));  // open: load, count, D, carry
  and and_1 (and_1_out, counter_1_q[0], counter_1_q[1]);
  // NOR_Gate nor_1 has open pins: in0=counter_1_q[0], in1=counter_1_q[1], out=open
  Button button_1 ();  // open: out
  Button button_2 ();  // open: out
  Button button_3 ();  // open: out
  Button button_4 ();  // open: out
  Button button_5 ();  // open: out
  Button button_6 ();  // open: out
  Button button_7 ();  // open: out
  Button button_8 ();  // open: out
  Button button_9 ();  // open: out
  Button button_10 ();  // open: out
  Button button_11 ();  // open: out
endmodule
