// Logisim project computer.circ as structural Verilog
module addsub_4bit (
  input  cin,
  input  [3:0] A,
  input  [3:0] B,
  input  sub,
  output [3:0] S,
  output [3:0] F
);

  wire adder_1_cout, adder_2_cout, adder_3_cout, xor_1_out, xor_2_out, xor_3_out, xor_4_out, xor_5_out;

  xor xor_1 (xor_1_out, cin, sub);
  xor xor_2 (xor_2_out, B[0], sub);
  xor xor_3 (xor_3_out, B[1], sub);
  xor xor_4 (xor_4_out, B[2], sub);
  xor xor_5 (xor_5_out, B[3], sub);
  Adder #(.width(1)) adder_1 (.a(A[0]), .b(xor_2_out), .out(S[0]), .cin(xor_1_out), .cout(adder_1_cout));
  Adder #(.width(1)) adder_2 (.a(A[1]), .b(xor_3_out), .out(S[1]), .cin(adder_1_cout), .cout(adder_2_cout));
  Adder #(.width(1)) adder_3 (.a(A[2]), .b(xor_4_out), .out(S[2]), .cin(adder_2_cout), .cout(adder_3_cout));
  Adder #(.width(1)) adder_4 (.a(A[3]), .b(xor_5_out), .out(F[1]), .cin(adder_3_cout), .cout(F[2]));
  and and_1 (F[0], ~S[0], ~S[1], ~S[2], ~F[1]);  // AND_Gate
  xor xor_6 (F[3], adder_3_cout, F[2]);

  assign S[3] = F[1];
endmodule

module addsub_4bit_test (
);

  wire dipswitch_2_sw1, dipswitch_4_sw1;
  wire [3:0] addsub_4bit_1_f, addsub_4bit_1_s, dipswitch_1_sw1, dipswitch_3_sw1;

  DipSwitch #(.number(4)) dipswitch_1 (
    .sw1(dipswitch_1_sw1[0]), .sw2(dipswitch_1_sw1[1]), .sw3(dipswitch_1_sw1[2]), .sw4(dipswitch_1_sw1[3]));
  DipSwitch #(.number(1)) dipswitch_2 (.sw1(dipswitch_2_sw1));
  DipSwitch #(.number(4)) dipswitch_3 (
    .sw1(dipswitch_3_sw1[0]), .sw2(dipswitch_3_sw1[1]), .sw3(dipswitch_3_sw1[2]), .sw4(dipswitch_3_sw1[3]));
  DipSwitch #(.number(1)) dipswitch_4 (.sw1(dipswitch_4_sw1));
  addsub_4bit addsub_4bit_1 (
    .cin(dipswitch_2_sw1), .A(dipswitch_1_sw1), .B(dipswitch_3_sw1), .sub(dipswitch_4_sw1),
    .S(addsub_4bit_1_s), .F(addsub_4bit_1_f));
  LedBar ledbar_1 (
    .led0(addsub_4bit_1_s[0]), .led1(addsub_4bit_1_s[1]), .led2(addsub_4bit_1_s[2]),
    .led3(addsub_4bit_1_s[3]), .led4(addsub_4bit_1_f[0]), .led5(addsub_4bit_1_f[1]),
    .led6(addsub_4bit_1_f[2]), .led7(addsub_4bit_1_f[3]));
endmodule

module full_adder (
  input  A,
  input  B,
  input  Cin,
  output S,
  output Cout
);

  wire and_1_out, and_2_out, xor_1_out;

  and and_1 (and_1_out, A, B);
  xor xor_1 (xor_1_out, A, B);
  xor xor_2 (S, xor_1_out, Cin);
  and and_2 (and_2_out, xor_1_out, Cin);
  or or_1 (Cout, and_2_out, and_1_out);
endmodule

module alu_4bit (
  input  Cin,
  input  [3:0] A,
  input  [3:0] B,
  input  [3:0] op,
  output [3:0] R,
  output [3:0] F
);

  wire and_1_out, and_2_out, and_3_out, multiplexer_1_out, or_1_out;
  wire [0:0] and_5_out, and_6_out, and_7_out, and_8_out;
  wire [3:0] addsub_4bit_1_f, addsub_4bit_1_s, and_4_out, not_1_out, or_2_out, xor_1_out;

  Multiplexer #(.select(4)) multiplexer_1 (
    .in0(1'b0), .in1(1'b0), .in2(Cin), .in3(Cin), .in4(1'b0), .in5(1'b0), .in6(1'b0), .in7(1'b0), .in8(1'b0),
    .in9(1'b0), .in10(1'b0), .in11(1'b0), .in12(1'b0), .in13(1'b0), .in14(1'b0), .in15(1'b0),
    .out(multiplexer_1_out), .sel(op));
  and and_1 (and_1_out, op[0], ~op[1], ~op[2], ~op[3]);  // AND_Gate
  and and_2 (and_2_out, op[0], op[1], ~op[2], ~op[3]);  // AND_Gate
  and and_3 (and_3_out, ~op[0], ~op[1], op[2], op[3]);  // AND_Gate
  or or_1 (or_1_out, and_1_out, and_2_out, and_3_out);
  assign and_4_out = A & B;  // AND_Gate and_4, 4 bits wide
  assign or_2_out = A | B;  // OR_Gate or_2, 4 bits wide
  assign xor_1_out = A ^ B;  // XOR_Gate xor_1, 4 bits wide
  assign not_1_out = ~A;  // NOT_Gate not_1, 4 bits wide
  and and_5 (and_5_out[0], ~A[0], ~A[1], ~A[2], ~A[3]);  // AND_Gate
  and and_6 (and_6_out[0], ~B[0], ~B[1], ~B[2], ~B[3]);  // AND_Gate
  and and_7 (and_7_out[0], ~B[0], ~B[1], ~B[2], ~B[3]);  // AND_Gate
  and and_8 (and_8_out[0], ~B[0], ~B[1], ~B[2], ~B[3]);  // AND_Gate
  addsub_4bit addsub_4bit_1 (
    .cin(multiplexer_1_out), .A(A), .B(B), .sub(or_1_out), .S(addsub_4bit_1_s), .F(addsub_4bit_1_f));
  Multiplexer #(.select(4), .width(4)) multiplexer_2 (
    .in0(addsub_4bit_1_s), .in1(addsub_4bit_1_s), .in2(addsub_4bit_1_s), .in3(addsub_4bit_1_s),
    .in4(and_4_out), .in5(or_2_out), .in6(xor_1_out), .in7(not_1_out), .in8({A[2:0], 1'b0}),
    .in9({1'b0, A[3:1]}), .in10({A[2:0], Cin}), .in11({Cin, A[3:1]}), .in12(addsub_4bit_1_s), .in13(A),
    .in14(B), .in15(4'b0000), .out(R), .sel(op));
  Multiplexer #(.select(4), .width(4)) multiplexer_3 (
    .in0(addsub_4bit_1_f), .in1(addsub_4bit_1_f), .in2(addsub_4bit_1_f), .in3(addsub_4bit_1_f),
    .in4({2'b00, A[3], and_5_out[0]}), .in5({2'b00, A[3], and_5_out[0]}), .in6({2'b00, A[3], and_5_out[0]}),
    .in7({2'b00, A[3], and_5_out[0]}), .in8({1'b0, {2{B[3]}}, and_7_out[0]}),
    .in9({1'b0, B[0], B[3], and_8_out[0]}), .in10({1'b0, {2{B[3]}}, and_7_out[0]}),
    .in11({1'b0, B[0], B[3], and_8_out[0]}), .in12(addsub_4bit_1_f), .in13({2'b00, A[3], and_5_out[0]}),
    .in14({2'b00, B[3], and_6_out[0]}), .in15(4'b0001), .out(F), .sel(op));
endmodule

module alu_4bit_test (
);

  wire dipswitch_1_sw1;
  wire [3:0] alu_4bit_1_f, alu_4bit_1_r, dipswitch_2_sw4, dipswitch_3_sw4, dipswitch_4_sw4;

  DipSwitch #(.number(1)) dipswitch_1 (.sw1(dipswitch_1_sw1));
  DipSwitch #(.number(4)) dipswitch_2 (
    .sw1(dipswitch_2_sw4[3]), .sw2(dipswitch_2_sw4[2]), .sw3(dipswitch_2_sw4[1]), .sw4(dipswitch_2_sw4[0]));
  Hex_Digit_Display hex_digit_display_1 (.value(dipswitch_2_sw4));  // open: dp
  Hex_Digit_Display hex_digit_display_2 (.value(dipswitch_3_sw4));  // open: dp
  DipSwitch #(.number(4)) dipswitch_3 (
    .sw1(dipswitch_3_sw4[3]), .sw2(dipswitch_3_sw4[2]), .sw3(dipswitch_3_sw4[1]), .sw4(dipswitch_3_sw4[0]));
  DipSwitch #(.number(4)) dipswitch_4 (
    .sw1(dipswitch_4_sw4[3]), .sw2(dipswitch_4_sw4[2]), .sw3(dipswitch_4_sw4[1]), .sw4(dipswitch_4_sw4[0]));
  alu_4bit alu_4bit_1 (
    .Cin(dipswitch_1_sw1), .A(dipswitch_2_sw4), .B(dipswitch_3_sw4), .op(dipswitch_4_sw4), .R(alu_4bit_1_r),
    .F(alu_4bit_1_f));
  LedBar #(.matrixcols(4)) ledbar_1 (
    .led0(alu_4bit_1_r[3]), .led1(alu_4bit_1_r[2]), .led2(alu_4bit_1_r[1]), .led3(alu_4bit_1_r[0]));
  Hex_Digit_Display hex_digit_display_3 (.value(alu_4bit_1_r));  // open: dp
  LedBar #(.matrixcols(4)) ledbar_2 (
    .led0(alu_4bit_1_f[3]), .led1(alu_4bit_1_f[2]), .led2(alu_4bit_1_f[1]), .led3(alu_4bit_1_f[0]));
endmodule
